# Fritzing sketch handheldspedo (saved by Fritzing 0.9.3b)
breadboards: 1

parts:
  Raspberry_Pi_1 = Raspberry Pi 3 [part_number=RPI-3-V1.2]
  Part1 = Triple Axis Accelerometer Breakout - ADXL345

nets:
  3V3: Raspberry_Pi_1.3v3, Part1.VCC
  N1: Raspberry_Pi_1.GPIO2, Part1.SDA
  N2: Raspberry_Pi_1.GPIO3, Part1.SCL
  GND: Raspberry_Pi_1.GND, Part1.GND

notes:
  Dariusz Kulpinski
  CENG 317
  Breadboard Wiring Diagram
  RED [VCC - 3.3V (Pin 1)]
  BLACK [GND - GND (Pin 38)]
  BLUE [SDA - SDA1 I2C (Pin 2)]
  YELLOW [SCL - SCL1 I2C (Pin 3)]
